// Logisim project RAM 8x11.circ as structural Verilog: 1 circuit, main circuit main
module main (
  input  [10:0] Entrada,
  input  [2:0] \Endereço ,
  input  WE
);

  wire and_1_out, and_2_out, and_3_out, and_4_out, and_5_out, and_6_out, and_7_out, and_8_out, and_9_out,
       and_10_out, and_11_out, and_12_out, and_13_out, and_14_out, and_15_out, and_16_out, d_ff_1_q,
       d_ff_2_q, d_ff_3_q, d_ff_4_q, d_ff_5_q, d_ff_6_q, d_ff_7_q, d_ff_8_q;

  and and_1 (and_1_out, ~\Endereço [2], ~\Endereço [1], ~\Endereço [0]);  // AND_Gate
  and and_2 (and_2_out, and_1_out, WE);
  and and_3 (and_3_out, ~\Endereço [2], ~\Endereço [1], \Endereço [0]);  // AND_Gate
  and and_4 (and_4_out, and_3_out, WE);
  and and_5 (and_5_out, ~\Endereço [2], \Endereço [1], ~\Endereço [0]);  // AND_Gate
  and and_6 (and_6_out, and_5_out, WE);
  and and_7 (and_7_out, ~\Endereço [2], \Endereço [1], \Endereço [0]);  // AND_Gate
  and and_8 (and_8_out, and_7_out, WE);
  and and_9 (and_9_out, \Endereço [2], ~\Endereço [1], ~\Endereço [0]);  // AND_Gate
  and and_10 (and_10_out, and_9_out, WE);
  and and_11 (and_11_out, \Endereço [2], ~\Endereço [1], \Endereço [0]);  // AND_Gate
  and and_12 (and_12_out, and_11_out, WE);
  and and_13 (and_13_out, \Endereço [2], \Endereço [1], ~\Endereço [0]);  // AND_Gate
  and and_14 (and_14_out, and_13_out, WE);
  and and_15 (and_15_out, \Endereço [2], \Endereço [1], \Endereço [0]);
  and and_16 (and_16_out, and_15_out, WE);
  D_Flip_Flop d_ff_1 (.clk(and_2_out), .D(Entrada[0]), .Q(d_ff_1_q));  // open: Qn, preset, en, reset
  D_Flip_Flop d_ff_2 (.clk(and_4_out), .D(Entrada[0]), .Q(d_ff_2_q));  // open: Qn, preset, en, reset
  D_Flip_Flop d_ff_3 (.clk(and_6_out), .D(Entrada[0]), .Q(d_ff_3_q));  // open: Qn, preset, en, reset
  D_Flip_Flop d_ff_4 (.clk(and_8_out), .D(Entrada[0]), .Q(d_ff_4_q));  // open: Qn, preset, en, reset
  D_Flip_Flop d_ff_5 (.clk(and_10_out), .D(Entrada[0]), .Q(d_ff_5_q));  // open: Qn, preset, en, reset
  D_Flip_Flop d_ff_6 (.clk(and_12_out), .D(Entrada[0]), .Q(d_ff_6_q));  // open: Qn, preset, en, reset
  D_Flip_Flop d_ff_7 (.clk(and_14_out), .D(Entrada[0]), .Q(d_ff_7_q));  // open: Qn, preset, en, reset
  D_Flip_Flop d_ff_8 (.clk(and_16_out), .D(Entrada[0]), .Q(d_ff_8_q));  // open: Qn, preset, en, reset
  // AND_Gate and_17 has open pins: in0=d_ff_1_q, in1=and_1_out, out=open
  // AND_Gate and_18 has open pins: in0=d_ff_2_q, in1=and_3_out, out=open
  // AND_Gate and_19 has open pins: in0=d_ff_3_q, in1=and_5_out, out=open
  // AND_Gate and_20 has open pins: in0=d_ff_4_q, in1=and_7_out, out=open
  // AND_Gate and_21 has open pins: in0=d_ff_5_q, in1=and_9_out, out=open
  // AND_Gate and_22 has open pins: in0=d_ff_6_q, in1=and_11_out, out=open
  // AND_Gate and_23 has open pins: in0=d_ff_7_q, in1=and_13_out, out=open
  // AND_Gate and_24 has open pins: in0=d_ff_8_q, in1=and_15_out, out=open
endmodule
