// Logisim project RAM.circ as structural Verilog: 1 circuit, main circuit main
module main (
  input  in_1,
  input  [1:0] A1A0,
  input  Write_Eneable,
  output out_4
);

  wire and_1_out, and_2_out, and_3_out, and_4_out, and_5_out, and_6_out, and_7_out, and_8_out, and_9_out,
       and_10_out, and_11_out, and_12_out, d_ff_1_q, d_ff_2_q, d_ff_3_q, d_ff_4_q;

  and and_1 (and_1_out, ~A1A0[1], ~A1A0[0]);  // AND_Gate
  and and_2 (and_2_out, and_1_out, Write_Eneable);
  and and_3 (and_3_out, ~A1A0[1], A1A0[0]);  // AND_Gate
  and and_4 (and_4_out, and_3_out, Write_Eneable);
  and and_5 (and_5_out, A1A0[1], ~A1A0[0]);  // AND_Gate
  and and_6 (and_6_out, and_5_out, Write_Eneable);
  and and_7 (and_7_out, A1A0[1], A1A0[0]);
  and and_8 (and_8_out, and_7_out, Write_Eneable);
  D_Flip_Flop d_ff_1 (.clk(and_2_out), .D(in_1), .Q(d_ff_1_q));  // open: Qn, preset, en, reset
  D_Flip_Flop d_ff_2 (.clk(and_4_out), .D(in_1), .Q(d_ff_2_q));  // open: Qn, preset, en, reset
  D_Flip_Flop d_ff_3 (.clk(and_6_out), .D(in_1), .Q(d_ff_3_q));  // open: Qn, preset, en, reset
  D_Flip_Flop d_ff_4 (.clk(and_8_out), .D(in_1), .Q(d_ff_4_q));  // open: Qn, preset, en, reset
  and and_9 (and_9_out, d_ff_1_q, and_1_out);
  and and_10 (and_10_out, d_ff_2_q, and_3_out);
  and and_11 (and_11_out, d_ff_3_q, and_5_out);
  and and_12 (and_12_out, d_ff_4_q, and_7_out);
  or or_1 (out_4, and_12_out, and_11_out, and_10_out, and_9_out);
endmodule
